// Logisim project zadaca.circ as structural Verilog
module osamkk (
  input  [2:0] ulaz,
  output [2:0] izlaz
);

  wire and_1_out, and_2_out, and_3_out, and_4_out, and_5_out, not_1_out, not_2_out, not_3_out;

  not not_1 (not_1_out, ulaz[2]);
  not not_2 (not_2_out, ulaz[1]);
  not not_3 (not_3_out, ulaz[0]);
  and and_1 (and_1_out, not_1_out, ulaz[0]);
  and and_2 (and_2_out, not_1_out, ulaz[1]);
  and and_3 (and_3_out, ulaz[2], not_2_out, not_3_out);
  and and_4 (and_4_out, not_2_out, ulaz[0]);
  and and_5 (and_5_out, ulaz[1], not_3_out);
  or or_1 (izlaz[2], and_1_out, and_2_out, and_3_out);
  or or_2 (izlaz[1], and_4_out, and_5_out);

  assign izlaz[0] = ulaz[0];
endmodule

module kolo32u1preko4u1 (
  input  [31:0] ulaz,
  input  [4:0] kontrola,
  output izlaz
);

  wire multiplexer_1_out, multiplexer_2_out, multiplexer_3_out, multiplexer_4_out, multiplexer_5_out,
       multiplexer_6_out, multiplexer_7_out, multiplexer_8_out, multiplexer_9_out, multiplexer_10_out;

  Multiplexer #(.select(2)) multiplexer_1 (
    .in0(ulaz[0]), .in1(ulaz[1]), .in2(ulaz[2]), .in3(ulaz[3]), .out(multiplexer_1_out), .sel(kontrola[1:0]));
  Multiplexer #(.select(2)) multiplexer_2 (
    .in0(ulaz[28]), .in1(ulaz[29]), .in2(ulaz[30]), .in3(ulaz[31]), .out(multiplexer_2_out),
    .sel(kontrola[1:0]));
  Multiplexer #(.select(2)) multiplexer_3 (
    .in0(ulaz[4]), .in1(ulaz[5]), .in2(ulaz[6]), .in3(ulaz[7]), .out(multiplexer_3_out), .sel(kontrola[1:0]));
  Multiplexer #(.select(2)) multiplexer_4 (
    .in0(ulaz[24]), .in1(ulaz[25]), .in2(ulaz[26]), .in3(ulaz[27]), .out(multiplexer_4_out),
    .sel(kontrola[1:0]));
  Multiplexer #(.select(2)) multiplexer_5 (
    .in0(ulaz[8]), .in1(ulaz[9]), .in2(ulaz[10]), .in3(ulaz[11]), .out(multiplexer_5_out), .sel(kontrola[1:0]));
  Multiplexer #(.select(2)) multiplexer_6 (
    .in0(ulaz[20]), .in1(ulaz[21]), .in2(ulaz[22]), .in3(ulaz[23]), .out(multiplexer_6_out),
    .sel(kontrola[1:0]));
  Multiplexer #(.select(2)) multiplexer_7 (
    .in0(ulaz[12]), .in1(ulaz[13]), .in2(ulaz[14]), .in3(ulaz[15]), .out(multiplexer_7_out),
    .sel(kontrola[1:0]));
  Multiplexer #(.select(2)) multiplexer_8 (
    .in0(ulaz[16]), .in1(ulaz[17]), .in2(ulaz[18]), .in3(ulaz[19]), .out(multiplexer_8_out),
    .sel(kontrola[1:0]));
  Multiplexer #(.select(2)) multiplexer_9 (
    .in0(multiplexer_1_out), .in1(multiplexer_3_out), .in2(multiplexer_5_out), .in3(multiplexer_7_out),
    .out(multiplexer_9_out), .sel(kontrola[3:2]));
  Multiplexer #(.select(2)) multiplexer_10 (
    .in0(multiplexer_8_out), .in1(multiplexer_6_out), .in2(multiplexer_4_out), .in3(multiplexer_2_out),
    .out(multiplexer_10_out), .sel(kontrola[3:2]));
  Multiplexer multiplexer_11 (.in0(multiplexer_9_out), .in1(multiplexer_10_out), .out(izlaz), .sel(kontrola[4]));
endmodule

module alu (
  input  [3:0] A,
  input  [3:0] B,
  input  [1:0] C,
  input  [1:0] K,
  input  M,
  output [3:0] decA,
  output [3:0] razlikaAiBdec,
  output [3:0] decB,
  output negativno,
  output [3:0] negiranA,
  output [3:0] ABnegirano,
  output [3:0] zbirAiBdec,
  output [3:0] tempBin,
  output [3:0] tempDec,
  output [3:0] izlaz
);

  wire fourbitadder_1_overflow;
  wire [3:0] fourbit2kk_1_complement, fourbit2kk_2_complement, fourbitadder_1_xplusy, nor_1_out, nor_2_out,
       nor_3_out, shifterudesno_1_shiftano, shifterulijevo_1_shiftano;

  assign negiranA = ~A;  // NOT_Gate not_1, 4 bits wide
  shifterUlijevo shifterulijevo_1 (.ulaz(tempBin), .K(K), .shiftano(shifterulijevo_1_shiftano));
  shifterUdesno shifterudesno_1 (.ulaz(tempBin), .K(K), .shiftano(shifterudesno_1_shiftano));
  fourbit2kk fourbit2kk_1 (.x(B), .complement(fourbit2kk_1_complement));
  assign nor_1_out = ~(A | A);  // NOR_Gate nor_1, 4 bits wide
  assign nor_2_out = ~(B | B);  // NOR_Gate nor_2, 4 bits wide
  fourbitadderNAND fourbitaddernand_1 (.x(A), .y(B), .xPlusy(zbirAiBdec));  // open: overflow
  Multiplexer #(.width(4)) multiplexer_1 (
    .in0(shifterulijevo_1_shiftano), .in1(shifterudesno_1_shiftano), .out(izlaz), .sel(M));
  fourbitadder fourbitadder_1 (
    .x(A), .y(fourbit2kk_1_complement), .xPlusy(fourbitadder_1_xplusy), .overflow(fourbitadder_1_overflow));
  assign nor_3_out = ~(nor_1_out | nor_2_out);  // NOR_Gate nor_3, 4 bits wide
  not not_2 (negativno, fourbitadder_1_overflow);
  assign ABnegirano = ~(nor_3_out | nor_3_out);  // NOR_Gate nor_4, 4 bits wide
  fourbit2kk fourbit2kk_2 (.x(fourbitadder_1_xplusy), .complement(fourbit2kk_2_complement));
  Multiplexer #(.width(4)) multiplexer_2 (
    .in0(fourbitadder_1_xplusy), .in1(fourbit2kk_2_complement), .out(razlikaAiBdec), .sel(negativno));
  Multiplexer #(.select(2), .width(4)) multiplexer_3 (
    .in0(razlikaAiBdec), .in1(negiranA), .in2(ABnegirano), .in3(zbirAiBdec), .out(tempBin), .sel(C));

  assign decA = A;
  assign decB = B;
  assign tempDec = tempBin;
endmodule

module fulladder (
  input  incarry,
  input  in1,
  input  in2,
  output out1,
  output outcarry
);

  wire and_1_out, and_2_out, xor_1_out;

  xor xor_1 (xor_1_out, in1, in2);
  and and_1 (and_1_out, in1, in2);
  xor xor_2 (out1, xor_1_out, incarry);
  and and_2 (and_2_out, incarry, xor_1_out);
  or or_1 (outcarry, and_2_out, and_1_out);
endmodule

module fourbitadder (
  input  [3:0] x,
  input  [3:0] y,
  output [3:0] xPlusy,
  output overflow
);

  wire fulladder_1_outcarry, fulladder_2_outcarry, fulladder_3_outcarry;

  fulladder fulladder_1 (.incarry(1'b0), .in1(x[0]), .in2(y[0]), .out1(xPlusy[0]), .outcarry(fulladder_1_outcarry));
  fulladder fulladder_2 (
    .incarry(fulladder_1_outcarry), .in1(x[1]), .in2(y[1]), .out1(xPlusy[1]), .outcarry(fulladder_2_outcarry));
  fulladder fulladder_3 (
    .incarry(fulladder_2_outcarry), .in1(x[2]), .in2(y[2]), .out1(xPlusy[2]), .outcarry(fulladder_3_outcarry));
  fulladder fulladder_4 (.incarry(fulladder_3_outcarry), .in1(x[3]), .in2(y[3]), .out1(xPlusy[3]), .outcarry(overflow));
endmodule

module fourbit2kk (
  input  [3:0] x,
  output [3:0] complement
);

  wire [3:0] not_1_out;

  assign not_1_out = ~x;  // NOT_Gate not_1, 4 bits wide
  fourbitadder fourbitadder_1 (.x(4'b0001), .y(not_1_out), .xPlusy(complement));  // open: overflow
endmodule

module fulladderNAND (
  input  incarry,
  input  in1,
  input  in2,
  output out1,
  output outcarry
);

  wire iksor_out_3, nand_1_out, nand_2_out, nand_3_out, nand_4_out;

  xorprekoNAND iksor (.in_1(in1), .in_2(in2), .out_3(iksor_out_3));
  nand nand_1 (nand_1_out, in1, in2);
  nand nand_2 (nand_2_out, nand_1_out, nand_1_out);
  xorprekoNAND iksor2 (.in_1(iksor_out_3), .in_2(incarry), .out_3(out1));
  nand nand_3 (nand_3_out, incarry, iksor_out_3);
  nand nand_4 (nand_4_out, nand_3_out, nand_3_out);
  iliprekoNAND ili (.in_1(nand_4_out), .in_2(nand_2_out), .out_3(outcarry));
endmodule

module iliprekoNAND (
  input  in_1,
  input  in_2,
  output out_3
);

  wire nand_1_out, nand_2_out;

  nand nand_1 (nand_1_out, in_1, in_1);
  nand nand_2 (nand_2_out, in_2, in_2);
  nand nand_3 (out_3, nand_1_out, nand_2_out);
endmodule

module xorprekoNAND (
  input  in_1,
  input  in_2,
  output out_3
);

  wire nand_1_out, nand_2_out, nand_3_out, nand_4_out, nand_5_out, nand_6_out;

  nand nand_1 (nand_1_out, in_1, in_1);
  nand nand_2 (nand_2_out, in_2, in_2);
  nand nand_3 (nand_3_out, nand_1_out, in_2);
  nand nand_4 (nand_4_out, nand_3_out, nand_3_out);
  nand nand_5 (nand_5_out, in_1, nand_2_out);
  nand nand_6 (nand_6_out, nand_5_out, nand_5_out);
  iliprekoNAND iliNAND (.in_1(nand_4_out), .in_2(nand_6_out), .out_3(out_3));
endmodule

module fourbitadderNAND (
  input  [3:0] x,
  input  [3:0] y,
  output [3:0] xPlusy,
  output overflow
);

  wire fulladdernand_1_outcarry, fulladdernand_2_outcarry, fulladdernand_3_outcarry;

  fulladderNAND fulladdernand_1 (
    .incarry(1'b0), .in1(x[0]), .in2(y[0]), .out1(xPlusy[0]), .outcarry(fulladdernand_1_outcarry));
  fulladderNAND fulladdernand_2 (
    .incarry(fulladdernand_1_outcarry), .in1(x[1]), .in2(y[1]), .out1(xPlusy[1]),
    .outcarry(fulladdernand_2_outcarry));
  fulladderNAND fulladdernand_3 (
    .incarry(fulladdernand_2_outcarry), .in1(x[2]), .in2(y[2]), .out1(xPlusy[2]),
    .outcarry(fulladdernand_3_outcarry));
  fulladderNAND fulladdernand_4 (
    .incarry(fulladdernand_3_outcarry), .in1(x[3]), .in2(y[3]), .out1(xPlusy[3]), .outcarry(overflow));
endmodule

module shifterUdesno (
  input  [3:0] ulaz,
  input  [1:0] K,
  output [3:0] shiftano
);

  Multiplexer #(.select(2)) multiplexer_1 (
    .in0(ulaz[0]), .in1(ulaz[1]), .in2(ulaz[2]), .in3(ulaz[3]), .out(shiftano[0]), .sel(K));
  Multiplexer #(.select(2)) multiplexer_2 (
    .in0(ulaz[1]), .in1(ulaz[2]), .in2(ulaz[3]), .in3(1'b0), .out(shiftano[1]), .sel(K));
  Multiplexer #(.select(2)) multiplexer_3 (
    .in0(ulaz[2]), .in1(ulaz[3]), .in2(1'b0), .in3(1'b0), .out(shiftano[2]), .sel(K));
  Multiplexer #(.select(2)) multiplexer_4 (
    .in0(ulaz[3]), .in1(1'b0), .in2(1'b0), .in3(1'b0), .out(shiftano[3]), .sel(K));
endmodule

module shifterUlijevo (
  input  [3:0] ulaz,
  input  [1:0] K,
  output [3:0] shiftano
);

  Multiplexer #(.select(2)) multiplexer_1 (
    .in0(ulaz[0]), .in1(1'b0), .in2(1'b0), .in3(1'b0), .out(shiftano[0]), .sel(K));
  Multiplexer #(.select(2)) multiplexer_2 (
    .in0(ulaz[1]), .in1(ulaz[0]), .in2(1'b0), .in3(1'b0), .out(shiftano[1]), .sel(K));
  Multiplexer #(.select(2)) multiplexer_3 (
    .in0(ulaz[2]), .in1(ulaz[1]), .in2(ulaz[0]), .in3(1'b0), .out(shiftano[2]), .sel(K));
  Multiplexer #(.select(2)) multiplexer_4 (
    .in0(ulaz[3]), .in1(ulaz[2]), .in2(ulaz[1]), .in3(ulaz[0]), .out(shiftano[3]), .sel(K));
endmodule
